// Logisim project adder.circ as structural Verilog: 1 circuit, main circuit main
module main (
);

  wire and_1_out, clock_1_out;
  wire [2:0] t_ff_3_q;

  Clock clock_1 (.out(clock_1_out));
  and and_1 (and_1_out, t_ff_3_q[1], t_ff_3_q[0]);
  T_Flip_Flop t_ff_1 (.clk(clock_1_out), .T(and_1_out), .Q(t_ff_3_q[2]));  // open: Qn, preset, reset, en
  T_Flip_Flop t_ff_2 (.clk(clock_1_out), .T(t_ff_3_q[0]), .Q(t_ff_3_q[1]));  // open: Qn, preset, reset, en
  T_Flip_Flop t_ff_3 (.clk(clock_1_out), .T(1'b1), .Q(t_ff_3_q[0]));  // open: Qn, preset, reset, en
  // Probe on t_ff_3_q
endmodule
