// Logisim project circut_2.circ as structural Verilog: 1 circuit, main circuit main
// 8
module main (
  input  _1,
  input  _2,
  input  _3,
  input  _4,
  output out_5,
  output out_6,
  output out_7,
  output out_8
);

  wire and_1_out, and_2_out, and_3_out, and_4_out, and_6_out, and_7_out, not_1_out, not_2_out, not_3_out,
       not_4_out;

  // Probe on {_1, _2, _3, _4}
  not not_1 (not_1_out, _1);
  not not_2 (not_2_out, _2);
  not not_3 (not_3_out, _3);
  not not_4 (not_4_out, _4);
  and and_1 (and_1_out, _1, not_2_out, not_3_out);
  and and_2 (and_2_out, not_1_out, _2);
  and and_3 (and_3_out, not_1_out, not_2_out);
  and and_4 (and_4_out, not_2_out, not_3_out);
  and and_5 (out_7, not_1_out, _3);
  and and_6 (and_6_out, not_2_out, not_3_out, _4);
  and and_7 (and_7_out, not_1_out, _4);
  or or_1 (out_5, and_1_out, and_2_out);
  or or_2 (out_6, and_3_out, and_4_out);
  or or_3 (out_8, and_6_out, and_7_out);
  // Probe on {out_5, out_6, out_7, out_8}
endmodule
